# Fritzing sketch tp-final (saved by Fritzing 0.9.8b)
breadboards: 1

parts:
  Raspberry_Pi_1 = Raspberry Pi 3 [part_number=RPI-3-V1.2]
  HC-SR04_Sensor_1 = HC-SR04 Ultrasonic Distance Sensor
  RHT1 = Humidity and Temperature Sensor RHT03
  Keypad4x1 = Keypad Membran 4x4

nets:
  GND: Raspberry_Pi_1.GND, HC-SR04_Sensor_1.GND, RHT1.GND_2
  N1: Raspberry_Pi_1.GPIO17, Keypad4x1.Pin8
  N2: Raspberry_Pi_1.GPIO27, Keypad4x1.Pin7
  N3: Raspberry_Pi_1.GPIO22, Keypad4x1.Pin6
  N4: Raspberry_Pi_1.GPIO10, Keypad4x1.Pin5
  N5: Raspberry_Pi_1.GPIO9, Keypad4x1.Pin4
  N6: Raspberry_Pi_1.GPIO11, Keypad4x1.Pin3
  N7: Raspberry_Pi_1.ID_SD, Keypad4x1.Pin2
  N8: Raspberry_Pi_1.GPIO5, Keypad4x1.Pin1
  N9: Raspberry_Pi_1.GPIO19, HC-SR04_Sensor_1.TRIG
  N10: Raspberry_Pi_1.GPIO26, HC-SR04_Sensor_1.ECHO
  N11: Raspberry_Pi_1.GPIO20, RHT1.Data-signal
  VCC: Raspberry_Pi_1.5V, HC-SR04_Sensor_1.VCC, RHT1.Vcc

custom parts:
  Keypad Membran 4x4: Membrane Keypad 4x4 Matrix
